# Fritzing sketch scootboot (saved by Fritzing 1.0.5)

parts:
  Part1 = Arduino Nano (Rev3.0) (ICSP)
  A1 = ELRS EP2 Receiver
  M1 = MDD10A
  V1 = DC Power [voltage=12V internal_resistance=0.1Ω]
  M2 = DC Motor [voltage_(max)=12V voltage_(min)=3V]
  M3 = DC Motor [voltage_(max)=12V voltage_(min)=3V]
  U1 = LM2596 step down module

nets:
  GND: Part1.GND, A1.GND, M1.Bat-, M1.GND, V1.V-, U1.IN-, U1.OUT-
  N1: Part1.D3, M1.DIR2
  N2: Part1.D4, M1.PWM2
  N3: Part1.D6, M1.DIR1
  N4: Part1.D7, M1.PWM1
  N5: Part1.D9, A1.TX
  N6: Part1.D10, A1.RX
  VIN: Part1.VIN, A1.5V, U1.OUT+
  N7: M1.M1B-1, M2.pin_1
  N8: M1.M1A1, M2.pin_2
  N9: M1.Bat+, V1.V+, U1.IN+
  N10: M1.M2A-1, M3.pin_1
  N11: M1.M2B-1, M3.pin_2

custom parts:
  ELRS EP2 Receiver: ELRS EP2 Receiver by HappyModel
  LM2596 step down module: LM2596 DC-DC step down power supply module 3 A.
